// Logisim project cpu.circ as structural Verilog: 6 circuits, main circuit main
// CPU
module main (
  input  [31:0] RS_READ_VALUE,
  input  [31:0] RI_READ_VALUE,
  input  [31:0] RD_READ_VALUE,
  input  [31:0] JC_READ_VALUE,
  input  [31:0] INSTRUCTION,
  input  CLOCK,
  output [4:0] RS,
  output [4:0] RI,
  output [4:0] RD,
  output [31:0] RD_WRITE_VALUE,
  output RD_WRITE_ENABLE,
  output [23:0] FETCH_ADDRESS
);

  wire _4, _5, _6, and_1_out, comparator_1_eq, comparator_2_eq, comparator_4_eq, comparator_5_eq,
       comparator_6_eq, comparator_7_eq, comparator_8_eq, comparator_9_eq, comparator_10_eq, dontwrite, jcb,
       jceq, jcs, jumpwrite, loadmem, multiplexer_5_out, multiplexer_12_out, pcselector, storemem, wholeword;
  wire [23:0] bit_extender_3_out, jpc, multiplexer_11_out, pcplusone;
  wire [24:0] addrinmem;
  wire [31:0] ALU_RESULT, ALU_WRITE_VALUE, bit_extender_2_out, datainmem, dataoutmem, JC_WRITE_VALUE,
       multiplexer_1_out, multiplexer_3_out, multiplexer_6_out, u_mem_1_data_out;

  Multiplexer #(.select(4), .width(32)) multiplexer_1 (
    .in10(ALU_RESULT), .in11(ALU_RESULT), .in12(ALU_RESULT), .in13(ALU_RESULT), .out(multiplexer_1_out),
    .sel(INSTRUCTION[31:28]));  // open: in0, in1, in2, in3, in4, in5, in6, in7, in8, in9, in14, in15, en
  Bit_Extender #(.in_width(32), .out_width(25)) bit_extender_1 (.in(multiplexer_1_out), .out(addrinmem));
  Multiplexer #(.select(4), .width(32)) multiplexer_2 (
    .in11(RD_READ_VALUE), .in13(RD_READ_VALUE), .out(datainmem), .sel(INSTRUCTION[31:28]));  // open: in0, in1, in2, in3, in4, in5, in6, in7, in8, in9, in10, in12, in14, in15, en
  assign bit_extender_2_out = {{15{INSTRUCTION[16]}}, INSTRUCTION[16:0]};  // Bit_Extender bit_extender_2
  Multiplexer #(.width(32)) multiplexer_3 (
    .in0(RI_READ_VALUE), .in1(bit_extender_2_out), .out(multiplexer_3_out), .sel(INSTRUCTION[27]));  // open: en
  and and_1 (and_1_out, dontwrite, multiplexer_5_out);
  or or_1 (RD_WRITE_ENABLE, and_1_out, jumpwrite);
  u_ALU u_alu_1 (
    .ALU_X(RS_READ_VALUE), .ALU_Y(multiplexer_3_out), .ALU_CONTROL(INSTRUCTION[31:28]),
    .ALU_RESULT(ALU_RESULT));
  Multiplexer #(.select(4), .width(32)) multiplexer_4 (
    .in0(ALU_RESULT), .in1(ALU_RESULT), .in2(ALU_RESULT), .in3(ALU_RESULT), .in4(ALU_RESULT),
    .in5(ALU_RESULT), .in6(ALU_RESULT), .in7(ALU_RESULT), .in8(ALU_RESULT), .in9(ALU_RESULT),
    .in10(ALU_RESULT), .in11(ALU_RESULT), .in12(ALU_RESULT), .in13(ALU_RESULT), .in14(ALU_RESULT),
    .out(ALU_WRITE_VALUE), .sel(INSTRUCTION[31:28]));  // open: in15, en
  Multiplexer #(.select(4)) multiplexer_5 (
    .in0(1'b1), .in1(1'b1), .in2(1'b1), .in3(1'b1), .in4(1'b1), .in5(1'b1), .in6(1'b1), .in7(1'b1),
    .in8(1'b1), .in9(1'b1), .in10(1'b1), .in11(1'b0), .in12(1'b1), .in13(1'b0), .in14(1'b1),
    .out(multiplexer_5_out), .sel(INSTRUCTION[31:28]));  // open: in15, en
  Comparator #(.width(4)) comparator_1 (.a(INSTRUCTION[31:28]), .b(4'b1111), .eq(comparator_1_eq));  // open: gt, lt
  Comparator #(.width(3)) comparator_2 (.a(INSTRUCTION[26:24]), .b(3'b111), .eq(comparator_2_eq));  // open: gt, lt
  Multiplexer #(.width(32)) multiplexer_6 (
    .in0(ALU_WRITE_VALUE), .in1(JC_WRITE_VALUE), .out(multiplexer_6_out), .sel(jumpwrite));  // open: en
  Bit_Extender #(.in_width(32), .out_width(24)) bit_extender_3 (.in(RI_READ_VALUE), .out(bit_extender_3_out));
  and and_2 (jumpwrite, comparator_1_eq, comparator_2_eq);
  assign JC_WRITE_VALUE = {{8{1'b0}}, pcplusone};  // Bit_Extender bit_extender_4
  Multiplexer #(.width(5)) multiplexer_7 (
    .in0(INSTRUCTION[26:22]), .in1(5'b00110), .out(RD), .sel(jumpwrite));  // open: en
  u_MEM u_mem_1 (
    .ADDRESS(addrinmem), .DATA_OUT(u_mem_1_data_out), .WORD_MODE(wholeword), .MEM_WRITE(storemem),
    .DATA_IN(datainmem), .CLOCK(CLOCK));
  Multiplexer #(.width(24)) multiplexer_8 (
    .in0(bit_extender_3_out), .in1(INSTRUCTION[23:0]), .out(jpc), .sel(INSTRUCTION[27]));  // open: en
  Comparator #(.width(32)) comparator_3 (.a(JC_READ_VALUE), .b({32{1'b0}}), .gt(jcb), .eq(jceq), .lt(jcs));
  or or_2 (_4, jceq, jcs);
  not not_1 (_5, jceq);
  or or_3 (_6, jcb, jceq);
  Multiplexer #(.width(32)) multiplexer_9 (
    .in0(multiplexer_6_out), .in1(dataoutmem), .out(RD_WRITE_VALUE), .sel(loadmem));  // open: en
  Multiplexer #(.select(4), .width(32)) multiplexer_10 (
    .in10(u_mem_1_data_out), .in12(u_mem_1_data_out), .out(dataoutmem), .sel(INSTRUCTION[31:28]));  // open: in0, in1, in2, in3, in4, in5, in6, in7, in8, in9, in11, in13, in14, in15, en
  Adder #(.width(24)) adder_1 (.a(FETCH_ADDRESS), .b(24'h1), .out(pcplusone));  // open: cin, cout
  Multiplexer #(.width(24)) multiplexer_11 (
    .in0(pcplusone), .in1(jpc), .out(multiplexer_11_out), .sel(pcselector));  // open: en
  Multiplexer #(.select(3)) multiplexer_12 (
    .in0(1'b1), .in1(jcb), .in2(jceq), .in3(jcs), .in4(_4), .in5(_5), .in6(_6), .in7(1'b1),
    .out(multiplexer_12_out), .sel(INSTRUCTION[26:24]));  // open: en
  Register #(.width(24)) register_1 (.D(multiplexer_11_out), .Q(FETCH_ADDRESS), .clk(CLOCK));  // open: en, clr
  Comparator #(.width(4)) comparator_4 (.a(INSTRUCTION[31:28]), .b(4'b1010), .eq(comparator_4_eq));  // open: gt, lt
  Comparator #(.width(4)) comparator_5 (.a(INSTRUCTION[31:28]), .b(4'b1100), .eq(comparator_5_eq));  // open: gt, lt
  Comparator #(.width(4)) comparator_6 (.a(INSTRUCTION[31:28]), .b(4'b1011), .eq(comparator_6_eq));  // open: gt, lt
  Comparator #(.width(4)) comparator_7 (.a(INSTRUCTION[31:28]), .b(4'b1101), .eq(comparator_7_eq));  // open: gt, lt
  Comparator #(.width(4)) comparator_8 (.a(INSTRUCTION[31:28]), .b(4'b1100), .eq(comparator_8_eq));  // open: gt, lt
  Comparator #(.width(4)) comparator_9 (.a(INSTRUCTION[31:28]), .b(4'b1101), .eq(comparator_9_eq));  // open: gt, lt
  Comparator #(.width(4)) comparator_10 (.a(INSTRUCTION[31:28]), .b(4'b1111), .eq(comparator_10_eq));  // open: gt, lt
  or or_4 (loadmem, comparator_4_eq, comparator_5_eq);
  or or_5 (storemem, comparator_6_eq, comparator_7_eq);
  or or_6 (wholeword, comparator_8_eq, comparator_9_eq);
  and and_3 (pcselector, multiplexer_12_out, comparator_10_eq);
  not not_2 (dontwrite, comparator_10_eq);

  assign RI = INSTRUCTION[4:0];
  assign RS = INSTRUCTION[21:17];

  // Other names for the same wires on the sheet: ADDR[23:0] = INSTRUCTION[23:0]; IMM[16:0] = INSTRUCTION[16:0];
  //   RD_INS[4:0] = INSTRUCTION[26:22]; JC[2:0] = INSTRUCTION[26:24]; I = INSTRUCTION[27];
  //   OP[3:0] = INSTRUCTION[31:28]

  // Notes on the sheet:
  //   Decoder
endmodule

module u_ALU (
  input  [31:0] ALU_X,
  input  [31:0] ALU_Y,
  input  [3:0] ALU_CONTROL,
  output [31:0] ALU_RESULT
);

  wire [4:0] bit_extender_1_out, bit_extender_4_out, bit_extender_5_out;
  wire [14:0] bit_extender_2_out;
  wire [16:0] bit_extender_3_out;
  wire [31:0] _00, _01, _02, _03, _04, _05, _06, _07, _08, _09, _14, bit_extender_6_out, bit_extender_7_out,
       shifter_1_out;

  Bit_Extender #(.in_width(32), .out_width(5)) bit_extender_1 (.in(ALU_Y), .out(bit_extender_1_out));
  Bit_Extender #(.in_width(32), .out_width(15)) bit_extender_2 (.in(ALU_X), .out(bit_extender_2_out));
  Bit_Extender #(.in_width(32), .out_width(17)) bit_extender_3 (.in(ALU_Y), .out(bit_extender_3_out));
  Bit_Extender #(.in_width(32), .out_width(5)) bit_extender_4 (.in(ALU_Y), .out(bit_extender_4_out));
  Bit_Extender #(.in_width(32), .out_width(5)) bit_extender_5 (.in(ALU_Y), .out(bit_extender_5_out));
  assign _02 = ALU_X & ALU_Y;  // AND_Gate and_1, 32 bits wide
  assign _03 = ALU_X | ALU_Y;  // OR_Gate or_1, 32 bits wide
  u_REV u_rev_1 (.INPUT(ALU_X), .REVERSE_AMOUNT(bit_extender_1_out), .OUTPUT(_04));
  assign _05 = ALU_X ^ ALU_Y;  // XOR_Gate xor_1, 32 bits wide
  Adder #(.width(32)) adder_1 (.a(ALU_X), .b(ALU_Y), .out(_06));  // open: cin, cout
  Subtractor #(.width(32)) subtractor_1 (.a(ALU_X), .b(ALU_Y), .out(_07));  // open: bin, bout
  Multiplier #(.width(32)) multiplier_1 (.a(ALU_X), .b(ALU_Y), .out(_08));  // open: cin, cout
  u_DIV u_div_1 (.in_1(ALU_X), .in_2(ALU_Y), .out_3(_09));
  assign bit_extender_6_out = {{15{1'b0}}, bit_extender_3_out};  // Bit_Extender bit_extender_6
  Shifter #(.width(32)) shifter_1 (.in(bit_extender_6_out), .\dist (5'b01111), .out(shifter_1_out));
  u_ARILSHIFT u_arilshift_1 (.in_1(ALU_X), .out_3(_00), .in_2(bit_extender_4_out));
  assign bit_extender_7_out = {{17{1'b0}}, bit_extender_2_out};  // Bit_Extender bit_extender_7
  Shifter #(.width(32), .shift("ar")) shifter_2 (.in(ALU_X), .\dist (bit_extender_5_out), .out(_01));
  Adder #(.width(32)) adder_2 (.a(bit_extender_7_out), .b(shifter_1_out), .out(_14));  // open: cin, cout
  Multiplexer #(.select(4), .width(32)) multiplexer_1 (
    .in0(_00), .in1(_01), .in2(_02), .in3(_03), .in4(_04), .in5(_05), .in6(_06), .in7(_07), .in8(_08),
    .in9(_09), .in10(_06), .in11(_06), .in12(_06), .in13(_06), .in14(_14), .out(ALU_RESULT), .sel(ALU_CONTROL));  // open: in15, en

  // Other names for the same wires on the sheet: result[31:0] = ALU_RESULT
endmodule

// Data Memory
module u_MEM (
  input  [24:0] ADDRESS,
  input  WORD_MODE,
  input  MEM_WRITE,
  input  [31:0] DATA_IN,
  input  CLOCK,
  output [31:0] DATA_OUT
);

  wire addrselector2, evenswitch, inputselector1, inputselector2, iseven, isodd, not_1_out, not_2_out,
       oddswitch;
  wire [15:0] first, last, multiplexer_1_out, multiplexer_2_out, ram_1_data, ram_2_data;
  wire [23:0] addrplusone, multiplexer_3_out, multiplexer_4_out, newaddr;
  wire [24:0] shifter_2_out;
  wire [31:0] evenodd, evenoutput, multiplexer_5_out, multiplexer_6_out, oddeven, oddoutput, shifter_1_out,
       shifter_3_out, shifter_4_out;

  or or_1 (oddswitch, WORD_MODE, isodd);
  or or_2 (evenswitch, WORD_MODE, iseven);
  and and_1 (addrselector2, WORD_MODE, not_1_out);
  not not_1 (not_1_out, iseven);
  and and_2 (inputselector1, WORD_MODE, iseven);
  not not_2 (not_2_out, iseven);
  Bit_Extender #(.in_width(25), .out_width(1)) bit_extender_1 (.in(ADDRESS), .out(isodd));
  and and_3 (inputselector2, WORD_MODE, not_2_out);
  not not_3 (iseven, isodd);
  Bit_Extender #(.in_width(32)) bit_extender_2 (.in(DATA_IN), .out(last));
  Bit_Extender #(.in_width(32)) bit_extender_3 (.in(shifter_1_out), .out(first));
  Shifter #(.width(32), .shift("lr")) shifter_1 (.in(DATA_IN), .\dist (5'b10000), .out(shifter_1_out));
  Bit_Extender #(.in_width(25), .out_width(24)) bit_extender_4 (.in(shifter_2_out), .out(newaddr));
  Shifter #(.width(25), .shift("lr")) shifter_2 (.in(ADDRESS), .\dist (5'b00001), .out(shifter_2_out));
  Adder #(.width(24)) adder_1 (.a(newaddr), .b(24'h1), .out(addrplusone));  // open: cin, cout
  Multiplexer #(.width(16)) multiplexer_1 (
    .in0(last), .in1(first), .out(multiplexer_1_out), .sel(inputselector1));  // open: en
  Multiplexer #(.width(16)) multiplexer_2 (
    .in0(last), .in1(first), .out(multiplexer_2_out), .sel(inputselector2));  // open: en
  Shifter #(.width(32)) shifter_3 (.in(oddoutput), .\dist (5'b10000), .out(shifter_3_out));
  Shifter #(.width(32)) shifter_4 (.in(evenoutput), .\dist (5'b10000), .out(shifter_4_out));
  Multiplexer #(.width(24)) multiplexer_3 (
    .in0(newaddr), .in1(addrplusone), .out(multiplexer_3_out), .sel(1'b0));  // open: en
  Multiplexer #(.width(24)) multiplexer_4 (
    .in0(newaddr), .in1(addrplusone), .out(multiplexer_4_out), .sel(addrselector2));  // open: en
  Adder #(.width(32)) adder_2 (.a(shifter_3_out), .b(evenoutput), .out(oddeven));  // open: cin, cout
  Adder #(.width(32)) adder_3 (.a(shifter_4_out), .b(oddoutput), .out(evenodd));  // open: cin, cout
  RAM #(.addrWidth(24), .dataWidth(16), .bus("separate")) ram_1 (
    .addr(multiplexer_3_out), .din(multiplexer_1_out), .data(ram_1_data), .str(MEM_WRITE), .sel(oddswitch),
    .clk(CLOCK));  // open: ld, clr
  RAM #(.addrWidth(24), .dataWidth(16), .bus("separate")) ram_2 (
    .addr(multiplexer_4_out), .din(multiplexer_2_out), .data(ram_2_data), .str(MEM_WRITE), .sel(evenswitch),
    .clk(CLOCK));  // open: ld, clr
  Multiplexer #(.width(32)) multiplexer_5 (
    .in0(oddoutput), .in1(evenoutput), .out(multiplexer_5_out), .sel(iseven));  // open: en
  Multiplexer #(.width(32)) multiplexer_6 (
    .in0(oddeven), .in1(evenodd), .out(multiplexer_6_out), .sel(isodd));  // open: en
  assign oddoutput = {{16{1'b0}}, ram_1_data};  // Bit_Extender bit_extender_5
  assign evenoutput = {{16{1'b0}}, ram_2_data};  // Bit_Extender bit_extender_6
  Multiplexer #(.width(32)) multiplexer_7 (
    .in0(multiplexer_5_out), .in1(multiplexer_6_out), .out(DATA_OUT), .sel(WORD_MODE));  // open: en

  // Other names for the same wires on the sheet: memwrite = MEM_WRITE; wordmode = WORD_MODE
endmodule

module u_REV (
  input  [31:0] INPUT,
  input  [4:0] REVERSE_AMOUNT,
  output [31:0] OUTPUT
);

  wire [4:0] and_1_out, and_2_out, and_3_out, and_4_out, and_5_out;
  wire [31:0] and_6_out, and_7_out, and_8_out, and_9_out, and_10_out, and_11_out, and_12_out, and_13_out,
       and_14_out, and_15_out, output1, output2, output3, output4, shifter_1_out, shifter_2_out,
       shifter_3_out, shifter_4_out, shifter_5_out, shifter_6_out, shifter_7_out, shifter_8_out,
       shifter_9_out, shifter_10_out;

  assign and_1_out = REVERSE_AMOUNT & 5'b00001;  // AND_Gate and_1, 5 bits wide
  assign and_2_out = REVERSE_AMOUNT & 5'b00010;  // AND_Gate and_2, 5 bits wide
  assign and_3_out = REVERSE_AMOUNT & 5'b00100;  // AND_Gate and_3, 5 bits wide
  assign and_4_out = REVERSE_AMOUNT & 5'b01000;  // AND_Gate and_4, 5 bits wide
  assign and_5_out = REVERSE_AMOUNT & 5'b10000;  // AND_Gate and_5, 5 bits wide
  assign and_6_out = 32'haaaaaaaa & shifter_1_out;  // AND_Gate and_6, 32 bits wide
  Shifter #(.width(32)) shifter_1 (.in(INPUT), .\dist (and_1_out), .out(shifter_1_out));
  Adder #(.width(32)) adder_1 (.a(and_6_out), .b(and_7_out), .out(output1));  // open: cin, cout
  assign and_7_out = 32'h55555555 & shifter_2_out;  // AND_Gate and_7, 32 bits wide
  Shifter #(.width(32), .shift("lr")) shifter_2 (.in(INPUT), .\dist (and_1_out), .out(shifter_2_out));
  assign and_8_out = 32'hcccccccc & shifter_3_out;  // AND_Gate and_8, 32 bits wide
  Adder #(.width(32)) adder_2 (.a(and_8_out), .b(and_10_out), .out(output2));  // open: cin, cout
  Shifter #(.width(32)) shifter_3 (.in(output1), .\dist (and_2_out), .out(shifter_3_out));
  assign and_9_out = 32'hffff0000 & shifter_4_out;  // AND_Gate and_9, 32 bits wide
  Shifter #(.width(32)) shifter_4 (.in(output4), .\dist (and_5_out), .out(shifter_4_out));
  assign and_10_out = 32'h33333333 & shifter_5_out;  // AND_Gate and_10, 32 bits wide
  Shifter #(.width(32), .shift("lr")) shifter_5 (.in(output1), .\dist (and_2_out), .out(shifter_5_out));
  Adder #(.width(32)) adder_3 (.a(and_9_out), .b(and_11_out), .out(OUTPUT));  // open: cin, cout
  assign and_11_out = 32'hffff & shifter_6_out;  // AND_Gate and_11, 32 bits wide
  Shifter #(.width(32), .shift("lr")) shifter_6 (.in(output4), .\dist (and_5_out), .out(shifter_6_out));
  assign and_12_out = 32'hf0f0f0f0 & shifter_7_out;  // AND_Gate and_12, 32 bits wide
  Shifter #(.width(32)) shifter_7 (.in(output2), .\dist (and_3_out), .out(shifter_7_out));
  Adder #(.width(32)) adder_4 (.a(and_12_out), .b(and_13_out), .out(output3));  // open: cin, cout
  assign and_13_out = 32'hf0f0f0f & shifter_8_out;  // AND_Gate and_13, 32 bits wide
  Shifter #(.width(32), .shift("lr")) shifter_8 (.in(output2), .\dist (and_3_out), .out(shifter_8_out));
  assign and_14_out = 32'hff00ff00 & shifter_9_out;  // AND_Gate and_14, 32 bits wide
  Adder #(.width(32)) adder_5 (.a(and_14_out), .b(and_15_out), .out(output4));  // open: cin, cout
  Shifter #(.width(32)) shifter_9 (.in(output3), .\dist (and_4_out), .out(shifter_9_out));
  assign and_15_out = 32'hff00ff & shifter_10_out;  // AND_Gate and_15, 32 bits wide
  Shifter #(.width(32), .shift("lr")) shifter_10 (.in(output3), .\dist (and_4_out), .out(shifter_10_out));
endmodule

module u_ARILSHIFT (
  input  [31:0] in_1,
  input  [4:0] in_2,
  output [31:0] out_3
);

  wire bit_extender_1_out;
  wire [31:0] adder_1_out, bit_extender_2_out, shifter_1_out, shifter_2_out, subtractor_1_out;

  Bit_Extender #(.in_width(32), .out_width(1)) bit_extender_1 (.in(in_1), .out(bit_extender_1_out));
  Shifter #(.width(32)) shifter_1 (.in(in_1), .\dist (in_2), .out(shifter_1_out));
  assign bit_extender_2_out = {{31{1'b0}}, bit_extender_1_out};  // Bit_Extender bit_extender_2
  Shifter #(.width(32)) shifter_2 (.in(bit_extender_2_out), .\dist (in_2), .out(shifter_2_out));
  Subtractor #(.width(32)) subtractor_1 (.a(shifter_2_out), .b(32'h1), .out(subtractor_1_out));  // open: bin, bout
  Multiplexer #(.width(32)) multiplexer_1 (
    .in0(shifter_1_out), .in1(adder_1_out), .out(out_3), .sel(bit_extender_1_out));  // open: en
  Adder #(.width(32)) adder_1 (.a(subtractor_1_out), .b(shifter_1_out), .out(adder_1_out));  // open: cin, cout
endmodule

module u_DIV (
  input  [31:0] in_1,
  input  [31:0] in_2,
  output [31:0] out_3
);

  wire _1b, _1eq, _1s, _2b, _2eq, _2s, and_1_out, doubleneg, normalselector;
  wire [31:0] adder_1_out, adder_2_out, adder_3_out, adder_4_out, divider_3_out, divider_4_out, inf,
       multiplexer_2_out, multiplexer_4_out, negneg, negpos, normal, not_1_out, not_2_out, not_3_out,
       not_4_out, not_5_out, not_6_out, oneposoneneg, posneg;

  Comparator #(.width(32)) comparator_1 (.a(in_1), .b({32{1'b0}}), .gt(_1b), .eq(_1eq), .lt(_1s));
  Comparator #(.width(32)) comparator_2 (.a(in_2), .b({32{1'b0}}), .gt(_2b), .eq(_2eq), .lt(_2s));
  assign not_1_out = ~in_1;  // NOT_Gate not_1, 32 bits wide
  assign not_2_out = ~in_2;  // NOT_Gate not_2, 32 bits wide
  assign not_3_out = ~in_1;  // NOT_Gate not_3, 32 bits wide
  assign not_4_out = ~in_2;  // NOT_Gate not_4, 32 bits wide
  Divider #(.width(32)) divider_1 (.a(in_1), .b(in_2), .out(normal));  // open: upper, rem
  Multiplexer #(.width(32)) multiplexer_1 (.in0(32'h7fffffff), .in1(32'h80000000), .out(inf), .sel(_1s));  // open: en
  Adder #(.width(32)) adder_1 (.a(not_1_out), .b(32'h1), .out(adder_1_out));  // open: cin, cout
  Adder #(.width(32)) adder_2 (.a(not_2_out), .b(32'h1), .out(adder_2_out));  // open: cin, cout
  Adder #(.width(32)) adder_3 (.a(not_3_out), .b(32'h1), .out(adder_3_out));  // open: cin, cout
  Adder #(.width(32)) adder_4 (.a(not_4_out), .b(32'h1), .out(adder_4_out));  // open: cin, cout
  Divider #(.width(32)) divider_2 (.a(adder_1_out), .b(adder_2_out), .out(negneg));  // open: upper, rem
  assign not_5_out = ~divider_3_out;  // NOT_Gate not_5, 32 bits wide
  Divider #(.width(32)) divider_3 (.a(adder_3_out), .b(in_2), .out(divider_3_out));  // open: upper, rem
  assign not_6_out = ~divider_4_out;  // NOT_Gate not_6, 32 bits wide
  Divider #(.width(32)) divider_4 (.a(in_1), .b(adder_4_out), .out(divider_4_out));  // open: upper, rem
  Adder #(.width(32)) adder_5 (.a(not_5_out), .b(32'h1), .out(negpos));  // open: cin, cout
  Adder #(.width(32)) adder_6 (.a(not_6_out), .b(32'h1), .out(posneg));  // open: cin, cout
  or or_1 (normalselector, _1eq, and_1_out);
  and and_1 (and_1_out, _1b, _2b);
  and and_2 (doubleneg, _1s, _2s);
  Multiplexer #(.width(32)) multiplexer_2 (
    .in0(oneposoneneg), .in1(negneg), .out(multiplexer_2_out), .sel(doubleneg));  // open: en
  Multiplexer #(.width(32)) multiplexer_3 (.in0(negpos), .in1(posneg), .out(oneposoneneg), .sel(_2s));  // open: en
  Multiplexer #(.width(32)) multiplexer_4 (
    .in0(multiplexer_2_out), .in1(inf), .out(multiplexer_4_out), .sel(_2eq));  // open: en
  Multiplexer #(.width(32)) multiplexer_5 (
    .in0(multiplexer_4_out), .in1(normal), .out(out_3), .sel(normalselector));  // open: en

  // Other names for the same wires on the sheet: infselector = _2eq; lower[31:0] = in_2; upper[31:0] = in_1
endmodule
